# Fritzing sketch lab-setup (saved by Fritzing 0.9.3b)
breadboards: 1

parts:
  Launchpad2 = TI Launchpad MSP430G2  # not connected
  U1 = 74HC595 [package="DIP16 [THT]"]
  LED2 = LED - 3mm [color="Red (633nm)" package="3 mm [THT]"]
  LED3 = LED - 3mm [color="Red (633nm)" package="3 mm [THT]"]
  LED4 = LED - 3mm [color="Red (633nm)" package="3 mm [THT]"]
  LED5 = LED - 3mm [color="Red (633nm)" package="3 mm [THT]"]
  R1 = Resistor [tolerance=±5% resistance=220 package=THT]
  R2 = Resistor [tolerance=±5% resistance=220 package=THT]
  R3 = Resistor [tolerance=±5% resistance=220 package=THT]
  R4 = Resistor [tolerance=±5% resistance=220 package=THT]

nets:
  N1: U1.Q1, LED4.anode
  N2: U1.Q2, LED3.anode
  N3: U1.Q3, LED5.anode
  N4: U1.GND, U1.OE, R1.Pin_1, R2.Pin_1, R3.Pin_1, R4.Pin_1
  N5: U1.MR, U1.VCC
  N6: U1.Q0, LED2.anode
  N7: LED2.cathode, R1.Pin_0
  N8: LED3.cathode, R3.Pin_0
  N9: LED4.cathode, R2.Pin_0
  N10: LED5.cathode, R4.Pin_0
