# Fritzing sketch Lesson27_Schematic (saved by Fritzing 0.9.2b)
breadboards: 1

parts:
  Launchpad2 = TI Launchpad MSP430G2
  C1 = Electrolytic Capacitor [capacitance=1µF package="100 mil [THT, electrolytic]"]
  R1 = Trimmer Potentiometer [maximum_resistance=10kΩ package=THT]
  TRS1 = Audio Jack (TRS) 3.5mm [package="4Ucon 08780 [THT]"]

nets:
  N1: Launchpad2.p14, C1.-
  N2: Launchpad2.p20, R1.leg2, TRS1.Sleeve
  N3: C1.+, R1.leg1
  N4: R1.wiper, TRS1.Ring, TRS1.Tip
