# Fritzing sketch Lab5_Schematic (saved by Fritzing 0.9.2b)
breadboards: 1

parts:
  Launchpad2 = TI Launchpad MSP430G2
  IR2 = TSOP312.., 314.. [package=THT]

nets:
  N1: Launchpad2.p1, IR2.Data
  N2: Launchpad2.p19, IR2.GND
  N3: Launchpad2.p20, IR2.Vs
