# Fritzing sketch lab-setup (saved by Fritzing 0.9.3b)
breadboards: 1

parts:
  Launchpad1 = TI Launchpad MSP430G2
  M1 = Dagu DGServo 9g (End View) [part_number=RS001B]
  R1 = Rotary Potentiometer (Small) [maximum_resistance=100kΩ package=THT]

nets:
  N1: Launchpad1.p10, M1.pulse
  N2: Launchpad1.p1, R1.leg2
  N3: Launchpad1.p14, R1.wiper
  N4: Launchpad1.p20, R1.leg1
