# Fritzing sketch Lesson27b_Schematic (saved by Fritzing 0.9.2b)
breadboards: 1

parts:
  Launchpad2 = TI Launchpad MSP430G2
  TRS1 = Audio Jack (TRS) 3.5mm [package="4Ucon 08780 [THT]"]
  C1 = Electrolytic Capacitor [capacitance=1µF package="100 mil [THT, electrolytic]"]

nets:
  N1: Launchpad2.p14, TRS1.Ring, TRS1.Tip, C1.+
  N2: Launchpad2.p20, TRS1.Sleeve, C1.-
